# Fritzing sketch fritzing (saved by Fritzing 0.9.3b)
perfboards: 1

parts:
  Part1 = Arduino Uno (Rev3)
  J1 = double row female pin header, 8 pins [form="♀ (female)"]
  J2 = double row female pin header, 8 pins [form="♀ (female)"]  # not connected
  J3 = Screw terminal - 2 pins [package=THT]  # not connected
  J4 = Screw terminal - 2 pins [package=THT]  # not connected
  J5 = Screw terminal - 2 pins [package=THT]  # not connected

nets:
  N1: Part1.D8, J1.pin3
  N2: Part1.D9_PWM, J1.pin4
  N3: Part1.D10_PWM/SS, J1.pin5
  N4: Part1.5V, J1.pin2
  N5: Part1.GND, J1.pin1

notes:
  GND
  VCC
  CH1
  SYNC
  CH2
  Krida 2CH Dimmer
  AC INPUT
  CHANNEL 1
  CHANNEL 2
